// Logisim project binary adder.circ as structural Verilog: 4 circuits, main circuit main
module main (
  input  in_1,
  input  in_2,
  input  in_3,
  input  in_4,
  input  in_5,
  input  in_6,
  input  in_7,
  input  in_8,
  input  in_9,
  output out_10,
  output out_11,
  output [3:0] out_12
);

  wire and_1_out_9, and_1_out_10, n4_bit_adder_1_out_14, n4_bit_adder_1_s1, n4_bit_adder_1_s2,
       n4_bit_adder_1_s3, n4_bit_adder_1_s4, or_gate_1_out_12;

  \and  and_1 (
    .in_2(n4_bit_adder_1_s4), .in_3(n4_bit_adder_1_s3), .in_7(n4_bit_adder_1_s4), .in_8(n4_bit_adder_1_s2),
    .out_9(and_1_out_9), .out_10(and_1_out_10));  // open: in_1, in_4, in_5, in_6, out_11, out_12
  or_gate or_gate_1 (
    .in_3(or_gate_1_out_12), .in_4(n4_bit_adder_1_out_14), .in_7(and_1_out_9), .in_8(and_1_out_10),
    .out_10(out_10), .out_12(or_gate_1_out_12));  // open: in_1, in_2, in_5, in_6, out_9, out_11
  _4_bit_adder u_4_bit_adder_1 (
    .in_1(in_2), .a1(in_3), .b1(in_4), .a2(in_5), .b2(in_6), .a3(in_7), .b3(in_8), .a4(in_9), .b4(in_1),
    .s1(n4_bit_adder_1_s1), .s2(n4_bit_adder_1_s2), .s3(n4_bit_adder_1_s3), .s4(n4_bit_adder_1_s4),
    .out_14(n4_bit_adder_1_out_14));
  _4_bit_adder u_4_bit_adder_2 (
    .in_1(in_1), .a1(out_10), .b1(out_10), .a2(in_1), .b2(n4_bit_adder_1_s4), .a3(n4_bit_adder_1_s2),
    .b3(n4_bit_adder_1_s3), .a4(n4_bit_adder_1_s1), .b4(in_1), .s1(out_12[0]), .s2(out_12[2]),
    .s3(out_12[1]), .s4(out_12[3]), .out_14(out_11));
endmodule

module \and  (
  input  in_1,
  input  in_2,
  input  in_3,
  input  in_4,
  input  in_5,
  input  in_6,
  input  in_7,
  input  in_8,
  output out_9,
  output out_10,
  output out_11,
  output out_12
);

  and and_1 (out_9, in_1, in_2);
  and and_2 (out_10, in_3, in_4);
  and and_3 (out_11, in_5, in_6);
  and and_4 (out_12, in_7, in_8);
endmodule

module or_gate (
  input  in_1,
  input  in_2,
  input  in_3,
  input  in_4,
  input  in_5,
  input  in_6,
  input  in_7,
  input  in_8,
  output out_9,
  output out_10,
  output out_11,
  output out_12
);

  or or_1 (out_9, in_1, in_2);
  or or_2 (out_10, in_3, in_4);
  or or_3 (out_11, in_5, in_6);
  or or_4 (out_12, in_7, in_8);
endmodule

module _4_bit_adder (
  input  in_1,
  input  a1,
  input  b1,
  input  a2,
  input  b2,
  input  a3,
  input  b3,
  input  a4,
  input  b4,
  output s1,
  output s2,
  output s3,
  output s4,
  output out_14
);

  wire adder_1_cout, adder_2_cout, adder_3_cout;

  Adder #(.width(1)) adder_1 (.a(a1), .b(b1), .out(s1), .cin(in_1), .cout(adder_1_cout));
  Adder #(.width(1)) adder_2 (.a(a2), .b(b2), .out(s2), .cin(adder_1_cout), .cout(adder_2_cout));
  Adder #(.width(1)) adder_3 (.a(a3), .b(b3), .out(s3), .cin(adder_2_cout), .cout(adder_3_cout));
  Adder #(.width(1)) adder_4 (.a(a4), .b(b4), .out(s4), .cin(adder_3_cout), .cout(out_14));
endmodule
