// Logisim project d flip flop.circ as structural Verilog: 1 circuit, main circuit main
module main (
  input  in_1,
  output [1:0] out_2
);

  wire clock_1_out, d_ff_2_qn, xor_1_out;

  ExactlyOne xor_1 (.out(xor_1_out), .in0(out_2[0]), .in1(in_1), .in2(out_2[1]));
  Clock clock_1 (.out(clock_1_out));
  D_Flip_Flop d_ff_1 (.clk(clock_1_out), .D(xor_1_out), .Q(out_2[0]));  // open: Qn, preset, en, reset
  D_Flip_Flop d_ff_2 (.clk(clock_1_out), .D(d_ff_2_qn), .Q(out_2[1]), .Qn(d_ff_2_qn));  // open: preset, en, reset

  // Notes on the sheet:
  //   D flip flop
endmodule
