// Logisim project jk flip flop.circ as structural Verilog: 1 circuit, main circuit main
module main (
  input  in_1,
  output [1:0] out_2
);

  wire clock_1_out, not_1_out, xor_1_out;

  not not_1 (not_1_out, in_1);
  xor xor_1 (xor_1_out, out_2[1], in_1);
  Clock clock_1 (.out(clock_1_out));
  J_K_Flip_Flop j_k_ff_1 (
    .J(xor_1_out), .clk(clock_1_out), .K(xor_1_out), .Q(out_2[0]));  // open: Qn, preset, en, reset
  J_K_Flip_Flop j_k_ff_2 (.J(1'b1), .clk(clock_1_out), .K(1'b1), .Q(out_2[1]));  // open: Qn, preset, en, reset

  // Notes on the sheet:
  //   jk flip flop
endmodule
