// Logisim project lab 3 minterm(task 3).circ as structural Verilog: 4 circuits, main circuit main
module main (
  input  A,
  input  B,
  input  C,
  output out_4
);

  wire and_1_out_11, and_2_out_11, and_3_out_11, not_1_out_8, not_1_out_9, not_2_out_8, not_2_out_10,
       not_3_out_9;

  Not not_1 (
    .in_2(A), .in_3(C), .out_8(not_1_out_8), .out_9(not_1_out_9));  // open: in_1, in_4, in_5, in_6, out_7, out_10, out_11, out_12
  Not not_2 (
    .in_2(A), .in_4(B), .out_8(not_2_out_8), .out_10(not_2_out_10));  // open: in_1, in_3, in_5, in_6, out_7, out_9, out_11, out_12
  Not not_3 (
    .in_3(C), .out_9(not_3_out_9));  // open: in_1, in_2, in_4, in_5, in_6, out_7, out_8, out_10, out_11, out_12
  \and  and_1 (
    .in_3(not_1_out_9), .in_4(not_1_out_8), .in_6(B), .out_11(and_1_out_11));  // open: in_1, in_2, in_5, in_7, in_8, in_9, out_10, out_12
  \and  and_2 (
    .in_3(not_2_out_10), .in_4(not_2_out_8), .in_5(C), .out_11(and_2_out_11));  // open: in_1, in_2, in_6, in_7, in_8, in_9, out_10, out_12
  \and  and_3 (
    .in_3(not_3_out_9), .in_5(B), .in_6(A), .out_11(and_3_out_11));  // open: in_1, in_2, in_4, in_7, in_8, in_9, out_10, out_12
  OR or_1 (
    .in_5(and_1_out_11), .out_11(out_4), .in_1(and_2_out_11), .in_3(and_3_out_11));  // open: in_4, in_6, out_10, in_2, in_7, in_8, out_12, in_9
endmodule

module OR (
  input  in_1,
  input  in_2,
  input  in_3,
  input  in_4,
  input  in_5,
  input  in_6,
  input  in_7,
  input  in_8,
  input  in_9,
  output out_10,
  output out_11,
  output out_12
);

  or or_1 (out_11, in_4, in_5, in_6);
  or or_2 (out_10, in_1, in_2, in_3);
  or or_3 (out_12, in_7, in_8, in_9);
endmodule

module Not (
  input  in_1,
  input  in_2,
  input  in_3,
  input  in_4,
  input  in_5,
  input  in_6,
  output out_7,
  output out_8,
  output out_9,
  output out_10,
  output out_11,
  output out_12
);

  not not_1 (out_7, in_1);
  not not_2 (out_8, in_2);
  not not_3 (out_9, in_3);
  not not_4 (out_10, in_4);
  not not_5 (out_11, in_5);
  not not_6 (out_12, in_6);
endmodule

module \and  (
  input  in_1,
  input  in_2,
  input  in_3,
  input  in_4,
  input  in_5,
  input  in_6,
  input  in_7,
  input  in_8,
  input  in_9,
  output out_10,
  output out_11,
  output out_12
);

  and and_1 (out_10, in_1, in_2, in_3);
  and and_2 (out_11, in_4, in_5, in_6);
  and and_3 (out_12, in_7, in_8, in_9);
endmodule
