// Logisim project prob 01.circ as structural Verilog: 4 circuits, main circuit main
module main (
  input  W,
  input  X,
  input  y,
  input  z,
  output A,
  output B,
  output c,
  output D
);

  wire and_1_out_9, and_3_out_9, and_4_out_9, and_5_out_9, and_6_out_9, and_7_out_9, not_1_out_5,
       not_3_out_5, not_4_out_5;

  \not  not_1 (.in_1(y), .out_5(not_1_out_5));  // open: in_2, in_3, in_4, out_6, out_7, out_8
  \not  not_2 (.in_1(z), .out_5(D));  // open: in_2, in_3, in_4, out_6, out_7, out_8
  \and  and_1 (
    .in_1(X), .in_2(z), .out_9(and_1_out_9));  // open: in_3, in_4, in_5, in_6, in_7, in_8, out_10, out_11, out_12
  \and  and_2 (.in_1(X), .in_2(y), .out_9(W));  // open: in_3, in_4, in_5, in_6, in_7, in_8, out_10, out_11, out_12
  \not  not_3 (.in_1(X), .out_5(not_3_out_5));  // open: in_2, in_3, in_4, out_6, out_7, out_8
  \not  not_4 (.in_1(z), .out_5(not_4_out_5));  // open: in_2, in_3, in_4, out_6, out_7, out_8
  \and  and_3 (
    .in_1(z), .in_2(y), .out_9(and_3_out_9));  // open: in_3, in_4, in_5, in_6, in_7, in_8, out_10, out_11, out_12
  \and  and_4 (
    .in_1(not_3_out_5), .in_2(z), .out_9(and_4_out_9));  // open: in_3, in_4, in_5, in_6, in_7, in_8, out_10, out_11, out_12
  \or  or_1 (
    .in_1(and_1_out_9), .in_2(W), .in_3(W), .out_9(A));  // open: in_4, in_5, in_6, in_7, in_8, out_10, out_11, out_12
  \and  and_5 (
    .in_1(y), .in_2(not_3_out_5), .out_9(and_5_out_9));  // open: in_3, in_4, in_5, in_6, in_7, in_8, out_10, out_11, out_12
  \and  and_6 (
    .in_1(not_4_out_5), .in_2(not_1_out_5), .in_3(X), .out_9(and_6_out_9));  // open: in_4, in_5, in_6, in_7, in_8, out_10, out_11, out_12
  \and  and_7 (
    .in_1(not_4_out_5), .in_2(not_1_out_5), .out_9(and_7_out_9));  // open: in_3, in_4, in_5, in_6, in_7, in_8, out_10, out_11, out_12
  \or  or_2 (
    .in_1(and_5_out_9), .in_2(and_4_out_9), .in_3(and_4_out_9), .in_5(and_6_out_9), .out_9(B));  // open: in_4, in_6, in_7, in_8, out_10, out_11, out_12
  \or  or_3 (
    .in_1(and_7_out_9), .in_2(and_3_out_9), .out_9(c));  // open: in_3, in_4, in_5, in_6, in_7, in_8, out_10, out_11, out_12
endmodule

module \and  (
  input  in_1,
  input  in_2,
  input  in_3,
  input  in_4,
  input  in_5,
  input  in_6,
  input  in_7,
  input  in_8,
  output out_9,
  output out_10,
  output out_11,
  output out_12
);

  and and_1 (out_9, in_1, in_2);
  and and_2 (out_10, in_3, in_4);
  and and_3 (out_11, in_5, in_6);
  and and_4 (out_12, in_7, in_8);
endmodule

module \or  (
  input  in_1,
  input  in_2,
  input  in_3,
  input  in_4,
  input  in_5,
  input  in_6,
  input  in_7,
  input  in_8,
  output out_9,
  output out_10,
  output out_11,
  output out_12
);

  or or_1 (out_9, in_1, in_2);
  or or_2 (out_10, in_3, in_4);
  or or_3 (out_11, in_5, in_6);
  or or_4 (out_12, in_7, in_8);
endmodule

module \not  (
  input  in_1,
  input  in_2,
  input  in_3,
  input  in_4,
  output out_5,
  output out_6,
  output out_7,
  output out_8
);

  not not_1 (out_5, in_1);
  not not_2 (out_6, in_2);
  not not_3 (out_7, in_3);
  not not_4 (out_8, in_4);
endmodule
