// Logisim project t flip flop.circ as structural Verilog: 1 circuit, main circuit main
module main (
  input  in_1,
  output [1:0] out_2
);

  wire clock_1_out, nor_1_out;

  nor nor_1 (nor_1_out, in_1, out_2[1]);
  Clock clock_1 (.out(clock_1_out));
  T_Flip_Flop t_ff_1 (.clk(clock_1_out), .T(nor_1_out), .Q(out_2[0]));  // open: Qn, preset, reset, en
  T_Flip_Flop t_ff_2 (.clk(clock_1_out), .T(1'b1), .Q(out_2[1]));  // open: Qn, preset, reset, en

  // Notes on the sheet:
  //   T flip flop
endmodule
